# Fritzing sketch SamplingCircuit (saved by Fritzing 1.0.2b)

parts:
  U2 = PSoC 5LP
  Q1 = MEMS
  U1 = ESP32S3
  Q2 = MEMS
  Q3 = MEMS
  Q4 = MEMS
  Q5 = MEMS
  Q6 = MEMS
  Q7 = MEMS
  Q8 = MEMS

nets:
  GND: U2.GND, Q1.GND, Q1.L/R, U1.GND, Q2.GND, Q2.L/R, Q3.GND, Q3.L/R, Q4.GND, Q4.L/R, Q5.GND, Q5.L/R, Q6.GND, Q6.L/R, Q7.GND, Q7.L/R, Q8.GND, Q8.L/R
  N1: U2.P3_0, Q2.DATA
  N2: U2.P3_1, Q2.WS
  N3: U2.P3_3, Q8.DATA
  N4: U2.P3_5, Q5.WS
  N5: U2.P3_6, Q5.DATA
  N6: U2.P15_0, Q4.WS
  N7: U2.P15_1, Q4.DATA
  N8: U2.P15_2, Q8.WS
  N9: U2.P15_3, Q7.DATA
  N10: U2.P0_1, Q7.WS
  N11: U2.P2_0, U1.GPIO10
  N12: U2.P2_1, U1.GPIO11
  N13: U2.P2_2, U1.GPIO12, U1.GPIO36, U1.GPIO42
  N14: U2.P2_3, U1.GPIO13
  N15: U2.P12_7, Q6.WS
  N16: U2.P12_6, Q6.DATA
  N17: U2.P12_3, Q1.WS
  SCK: U2.P12_2, Q1.SCK, Q2.SCK, Q3.SCK, Q4.SCK, Q5.SCK, Q6.SCK, Q7.SCK, Q8.SCK
  N18: U2.P12_1, Q1.DATA
  N19: U2.P1_4, Q3.WS
  N20: U2.P1_5, Q3.DATA
  VDD: U2.VDDIO, Q1.VDD, U1.3.3, Q2.VDD, Q3.VDD, Q4.VDD, Q5.VDD, Q6.VDD, Q7.VDD, Q8.VDD

custom parts:
  MEMS: Mems mic
  ESP32S3: s3
